# Fritzing sketch Simblee Lilypad Fitness Tracker (saved by Fritzing 0.9.2b)

parts:
  PART1 = LilyPad Pixel Board [part_number=DEV-11891]
  Part1 = LilyPad Accelerometer ADXL335
  Part2 = LilyPad Slide Switch
  Lilypad_Vibe1 = Lilypad Vibe Motor
  Lilypad_Vibe2 = Lilypad Vibe Motor
  Part4 = LilyPad Simblee

nets:
  VCC: PART1.VCC, Part1.5V, Part4.VCC
  GND: PART1.GND, Part1.COM, Part2.OFF, Lilypad_Vibe1.GND, Lilypad_Vibe2.GND, Part4.GND
  N1: PART1.DI, Part4.9
  N2: Part1.XOUT, Part4.5
  N3: Part1.YOUT, Part4.3
  N4: Part2.ON, Part4.15
  N5: Lilypad_Vibe1.Supply, Part4.11
  N6: Lilypad_Vibe2.Supply, Part4.12

notes:
  Pulse Sensor

custom parts:
  LilyPad Pixel Board: We know you love adding color to your e-textiles, adding the LilyPad Pixel Board to your project will only make it better. The pixel board is equipped with a WS2812 which is actually an RGB LED with a WS2811 built right into the LED! Several of these breakouts can be chained together to form a display or an addressable string. LilyPad is a wearable technology developed by Leah Buechley and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
